// Logisim project para_praticar1.circ as structural Verilog: 1 circuit, main circuit main
module main (
);

  wire and_1_out, and_2_out, not_1_out, not_2_out, not_3_out, not_4_out, or_1_out, undriven, undriven_2,
       undriven_3, undriven_4;

  or or_1 (or_1_out, undriven_2, undriven);
  not not_1 (not_1_out, undriven);
  not not_2 (not_2_out, undriven_2);
  and and_1 (and_1_out, not_1_out, not_2_out, not_3_out);
  not not_3 (not_3_out, undriven_3);
  and and_2 (and_2_out, or_1_out, not_4_out);
  not not_4 (not_4_out, undriven_4);

  // Notes on the sheet:
  //   Fe
  //   L
  //   U
  //   Fd
  //   A
  //   B
endmodule
