// Logisim project logisim.circ as structural Verilog: 8 circuits, main circuit main
module main (
  input  A,
  input  B,
  input  C,
  input  D
);

  wire and_1_out, and_2_out, and_3_out, and_4_out, not_1_out, not_2_out, not_3_out, not_4_out, or_1_out;

  and and_1 (and_1_out, B, not_1_out);
  not not_1 (not_1_out, D);
  not not_2 (not_2_out, B);
  and and_2 (and_2_out, not_2_out, D);
  not not_3 (not_3_out, A);
  not not_4 (not_4_out, C);
  or or_1 (or_1_out, and_1_out, and_2_out);
  and and_3 (and_3_out, not_3_out, not_4_out);
  and and_4 (and_4_out, or_1_out, and_3_out);

  // Notes on the sheet:
  //   YA
endmodule

module YA (
  input  A,
  input  B,
  input  C,
  input  D
);

  wire and_1_out, and_2_out, and_3_out, and_4_out, not_1_out, not_2_out, not_3_out, not_4_out, or_1_out;

  and and_1 (and_1_out, B, not_1_out);
  not not_1 (not_1_out, D);
  not not_2 (not_2_out, B);
  and and_2 (and_2_out, not_2_out, D);
  not not_3 (not_3_out, A);
  not not_4 (not_4_out, C);
  or or_1 (or_1_out, and_1_out, and_2_out);
  and and_3 (and_3_out, not_3_out, not_4_out);
  and and_4 (and_4_out, or_1_out, and_3_out);

  // Notes on the sheet:
  //   YA
endmodule

module YB (
  input  A,
  input  B,
  input  C,
  input  D
);

  wire and_1_out, and_2_out, and_3_out, and_5_out, not_1_out, not_2_out, not_3_out, or_1_out;

  not not_1 (not_1_out, C);
  and and_1 (and_1_out, not_1_out, D);
  and and_2 (and_2_out, C, not_2_out);
  not not_2 (not_2_out, D);
  or or_1 (or_1_out, and_1_out, and_2_out);
  not not_3 (not_3_out, A);
  and and_3 (and_3_out, not_3_out, B);
  // AND_Gate and_4 is placed but not wired
  // OR_Gate or_2 is placed but not wired
  and and_5 (and_5_out, or_1_out, and_3_out);
  // NOT_Gate not_4 is placed but not wired

  // Notes on the sheet:
  //   YB
endmodule

module YC (
  input  A,
  input  B,
  input  C,
  input  D
);

  wire and_1_out, and_2_out, and_4_out, not_1_out, not_2_out, not_3_out;

  not not_1 (not_1_out, D);
  and and_1 (and_1_out, not_1_out, C);
  not not_2 (not_2_out, B);
  and and_2 (and_2_out, not_2_out, not_3_out);
  not not_3 (not_3_out, A);
  // AND_Gate and_3 is placed but not wired
  // OR_Gate or_1 is placed but not wired
  and and_4 (and_4_out, and_1_out, and_2_out);
  // NOT_Gate not_4 is placed but not wired

  // Notes on the sheet:
  //   YC
endmodule

module YD (
  input  A,
  input  B,
  input  C,
  input  D
);

  wire and_1_out, and_2_out, and_3_out, and_4_out, and_5_out, and_6_out, and_8_out, not_1_out, not_2_out,
       not_3_out, not_4_out, not_6_out, or_1_out, or_3_out;

  not not_1 (not_1_out, C);
  and and_1 (and_1_out, not_1_out, not_2_out);
  not not_2 (not_2_out, D);
  and and_2 (and_2_out, D, not_3_out);
  not not_3 (not_3_out, C);
  and and_3 (and_3_out, D, C);
  and and_4 (and_4_out, and_1_out, B);
  and and_5 (and_5_out, and_2_out, not_4_out);
  not not_4 (not_4_out, B);
  and and_6 (and_6_out, and_3_out, B);
  // AND_Gate and_7 is placed but not wired
  or or_1 (or_1_out, and_4_out, and_5_out);
  // OR_Gate or_2 is placed but not wired
  or or_3 (or_3_out, or_1_out, and_6_out);
  // NOT_Gate not_5 is placed but not wired
  and and_8 (and_8_out, or_3_out, not_6_out);
  not not_6 (not_6_out, A);

  // Notes on the sheet:
  //   YD
endmodule

module YE (
  input  A,
  input  B,
  input  C,
  input  D
);

  wire and_1_out, and_2_out, and_3_out, and_4_out, and_5_out, not_1_out, not_2_out, not_3_out, not_4_out,
       not_5_out, or_1_out, or_2_out;

  not not_1 (not_1_out, A);
  not not_2 (not_2_out, A);
  not not_3 (not_3_out, C);
  and and_1 (and_1_out, D, not_1_out);
  and and_2 (and_2_out, not_2_out, B);
  not not_4 (not_4_out, C);
  and and_3 (and_3_out, D, not_3_out);
  not not_5 (not_5_out, B);
  and and_4 (and_4_out, and_2_out, not_4_out);
  and and_5 (and_5_out, and_3_out, not_5_out);
  or or_1 (or_1_out, and_1_out, and_4_out);
  or or_2 (or_2_out, or_1_out, and_5_out);

  // Notes on the sheet:
  //   YE
endmodule

module YF (
  input  A,
  input  B,
  input  C,
  input  D
);

  wire and_1_out, and_2_out, and_3_out, and_5_out, not_1_out, not_2_out, not_4_out, or_1_out, or_2_out;

  not not_1 (not_1_out, B);
  not not_2 (not_2_out, B);
  and and_1 (and_1_out, not_1_out, D);
  and and_2 (and_2_out, not_2_out, C);
  and and_3 (and_3_out, D, C);
  or or_1 (or_1_out, and_1_out, and_2_out);
  // NOT_Gate not_3 is placed but not wired
  or or_2 (or_2_out, or_1_out, and_3_out);
  // AND_Gate and_4 is placed but not wired
  and and_5 (and_5_out, or_2_out, not_4_out);
  not not_4 (not_4_out, A);
  // OR_Gate or_3 is placed but not wired

  // Notes on the sheet:
  //   YF
endmodule

module YG (
  input  A,
  input  B,
  input  C,
  input  D
);

  wire and_1_out, and_2_out, and_3_out, and_4_out, not_1_out, not_2_out, not_3_out, or_1_out;

  not not_1 (not_1_out, C);
  and and_1 (and_1_out, not_1_out, not_2_out);
  not not_2 (not_2_out, B);
  and and_2 (and_2_out, D, C);
  and and_3 (and_3_out, and_2_out, B);
  or or_1 (or_1_out, and_1_out, and_3_out);
  and and_4 (and_4_out, or_1_out, not_3_out);
  not not_3 (not_3_out, A);

  // Notes on the sheet:
  //   YG
endmodule
