// Logisim project pratica.circ as structural Verilog
module pratica12_1 (
  input  R,
  input  S
);

  wire nand_1_out, nand_2_out;

  nand nand_1 (nand_1_out, R, nand_2_out);
  nand nand_2 (nand_2_out, nand_1_out, S);
  LED led_1 (.in(nand_1_out));
  LED led_2 (.in(nand_2_out));

  // Notes on the sheet:
  //   Q
  //   ~Q
endmodule

module pratica12_2 (
  input  S,
  input  c,
  input  R
);

  wire nand_1_out, nand_2_out, nand_3_out, nand_4_out;

  nand nand_1 (nand_1_out, S, c);
  nand nand_2 (nand_2_out, c, R);
  nand nand_3 (nand_3_out, nand_1_out, nand_4_out);
  nand nand_4 (nand_4_out, nand_3_out, nand_2_out);
  LED led_1 (.in(nand_3_out));
  LED led_2 (.in(nand_4_out));

  // Notes on the sheet:
  //   Q
  //   ~Q
endmodule

module pratica12_3 (
  input  D
);

  wire nand_1_out, nand_2_out, not_1_out;

  not not_1 (not_1_out, D);
  nand nand_1 (nand_1_out, D, nand_2_out);
  nand nand_2 (nand_2_out, nand_1_out, not_1_out);
  LED led_1 (.in(nand_1_out));
  LED led_2 (.in(nand_2_out));

  // Notes on the sheet:
  //   Q
  //   ~Q
endmodule
